// Logisim project Questão 2 - Multiplexador.circ as structural Verilog: 1 circuit, main circuit main
module main (
  input  [3:0] in_1,
  input  [1:0] in_2,
  output S
);

  wire _00_out, _01_out, _10_out, _11_out, and_1_out, and_2_out, and_3_out, and_4_out, not_1_out, not_2_out,
       not_3_out, not_4_out;

  not not_1 (not_1_out, in_2[1]);
  not not_2 (not_2_out, in_2[0]);
  not not_3 (not_3_out, in_2[1]);
  not not_4 (not_4_out, in_2[0]);
  and _00 (_00_out, not_1_out, not_2_out);
  and _01 (_01_out, not_3_out, in_2[0]);
  and _10 (_10_out, in_2[1], not_4_out);
  and _11 (_11_out, in_2[0], in_2[1]);
  and and_1 (and_1_out, in_1[0], _00_out);
  and and_2 (and_2_out, in_1[1], _01_out);
  and and_3 (and_3_out, in_1[2], _10_out);
  and and_4 (and_4_out, in_1[3], _11_out);
  or or_1 (S, and_1_out, and_2_out, and_3_out, and_4_out);
endmodule
